# Fritzing sketch AtlasScientific_DO_Nano (saved by Fritzing 0.9.2b)
breadboards: 1

parts:
  Pre-Assembled_Female_BNC1 = Pre-Assembled Female BNC
  D_O_Circuit1 = D.O. Circuit
  Part3 = Arduino Nano (Rev3.0)

nets:
  VCC: Pre-Assembled_Female_BNC1.NC, D_O_Circuit1.Vcc, Part3.5V
  N1: Pre-Assembled_Female_BNC1.PRB, D_O_Circuit1.PRB
  N2: Pre-Assembled_Female_BNC1.GND, D_O_Circuit1.GND#5
  N3: D_O_Circuit1.GND#0, Part3.GND
  N4: D_O_Circuit1.TX, Part3.D7
  N5: D_O_Circuit1.RX, Part3.D8
