# Fritzing sketch AtlasScientific_DO_ProMini (saved by Fritzing 0.9.2b)
breadboards: 1

parts:
  Part2 = Arduino Pro Mini v13
  Pre-Assembled_Female_BNC1 = Pre-Assembled Female BNC
  D_O_Circuit1 = D.O. Circuit

nets:
  N1: Part2.GND, D_O_Circuit1.GND#0
  VCC: Part2.VCC, Pre-Assembled_Female_BNC1.NC, D_O_Circuit1.Vcc
  N2: Part2.D8, D_O_Circuit1.RX
  N3: Part2.D7, D_O_Circuit1.TX
  N4: Pre-Assembled_Female_BNC1.PRB, D_O_Circuit1.PRB
  N5: Pre-Assembled_Female_BNC1.GND, D_O_Circuit1.GND#5
