# Fritzing sketch ESP8266_ProMini (saved by Fritzing 0.9.2b)
breadboards: 1

parts:
  U1 = ESP8266 WiFi Module [part_number=ESP8266]
  Part1 = Arduino Pro Mini v13
  Part3 = FTDI Basic Programmer

nets:
  N1: U1.RXD, Part1.D4
  VCC: U1.VCC, U1.CH_PD, Part1.VCC, Part3.POWER
  GND: U1.GND, Part1.GND, Part3.CTS, Part3.GND
  N2: U1.TXD, Part1.D3_PWM
  N3: Part1.DTR, Part3.DTR
  N4: Part1.D0/TX, Part3.RXI
  N5: Part1.D1/RX, Part3.TXO

custom parts:
  ESP8266 WiFi Module: Generic WiFi Module based on the ESP8266 with onboard PCB antenna and UART communications
