# Fritzing sketch Thermistor_Nano (saved by Fritzing 0.9.2b)
breadboards: 1

parts:
  R1 = Resistor [tolerance=±5% resistance=10k package=THT]
  R2 = Temperature Sensor (Thermistor) [thermistor_type=NTC package=THT]
  Part3 = Arduino Nano (Rev3.0)

nets:
  N1: R1.Pin_0, Part3.5V
  N2: R1.Pin_1, R2.pin_1, Part3.A0
  N3: R2.pin_0, Part3.GND
