# Fritzing sketch Thermistor_ProMini (saved by Fritzing 0.9.2b)
breadboards: 1

parts:
  R1 = Resistor [tolerance=±5% resistance=10k package=THT]
  Part2 = Arduino Pro Mini v13
  R2 = Temperature Sensor (Thermistor) [thermistor_type=NTC package=THT]

nets:
  N1: R1.Pin_0, Part2.VCC
  N2: R1.Pin_1, Part2.A0, R2.pin_0
  N3: Part2.GND, R2.pin_1
