# Fritzing sketch WaterConductivity_Nano (saved by Fritzing 0.9.2b)
breadboards: 1

parts:
  R1 = Resistor [tolerance=±5% resistance=10k package=THT]
  Part3 = Arduino Nano (Rev3.0)

nets:
  N1: R1.Pin_0, Part3.A0
  N2: R1.Pin_1, Part3.GND

notes:
  To Probe
