# Fritzing sketch WaterConductivity_ProMini (saved by Fritzing 0.9.2b)
breadboards: 1

parts:
  R1 = Resistor [tolerance=±5% resistance=10k package=THT]
  Part2 = Arduino Pro Mini v13

nets:
  N1: R1.Pin_0, Part2.A0
  N2: R1.Pin_1, Part2.GND

notes:
  To Probe
