# Fritzing sketch AtlasScientific_pH_Nano (saved by Fritzing 0.9.2b)
breadboards: 1

parts:
  pH_Circuit1 = pH Circuit
  Pre-Assembled_Female_BNC1 = Pre-Assembled Female BNC
  Part3 = Arduino Nano (Rev3.0)

nets:
  N1: pH_Circuit1.GND#0, Part3.GND
  N2: pH_Circuit1.TX, Part3.D9
  N3: pH_Circuit1.RX, Part3.D10
  VCC: pH_Circuit1.Vcc, Pre-Assembled_Female_BNC1.NC, Part3.5V
  N4: pH_Circuit1.PRB, Pre-Assembled_Female_BNC1.PRB
  N5: pH_Circuit1.GND#5, Pre-Assembled_Female_BNC1.GND
