# Fritzing sketch AtlasScientific_pH_ProMini (saved by Fritzing 0.9.2b)
breadboards: 1

parts:
  pH_Circuit1 = pH Circuit
  Pre-Assembled_Female_BNC1 = Pre-Assembled Female BNC
  Part2 = Arduino Pro Mini v13

nets:
  N1: pH_Circuit1.GND#0, Part2.GND
  N2: pH_Circuit1.TX, Part2.D9_PWM
  N3: pH_Circuit1.RX, Part2.D10_PWM/SS
  VCC: pH_Circuit1.Vcc, Pre-Assembled_Female_BNC1.NC, Part2.A5, Part2.VCC
  N4: pH_Circuit1.PRB, Pre-Assembled_Female_BNC1.PRB
  N5: pH_Circuit1.GND#5, Pre-Assembled_Female_BNC1.GND
  N6: Part2.A4, Part2.A3
